# Fritzing sketch tessel-rgb-led-rainbow (saved by Fritzing 0.9.2b)
breadboards: 1

parts:
  Part1 = Tessel 2
  LED1 = RGB LED (com. cathode, rgb) [package="5 mm [THT]"]
  R1 = Resistor [tolerance=±5% resistance=220 package=THT]
  R2 = Resistor [tolerance=±5% resistance=220 package=THT]
  R3 = Resistor [tolerance=±5% resistance=220 package=THT]

nets:
  N1: Part1.5#35, R1.Pin_1
  N2: Part1.3V3, LED1.common_cathode
  N3: Part1.5#75, R2.Pin_1
  N4: Part1.6, R3.Pin_1
  N5: LED1.red_anode, R1.Pin_0
  N6: LED1.green_anode, R2.Pin_0
  N7: LED1.blue_anode, R3.Pin_0

custom parts:
  Tessel 2: Draft version of Tessel 2
